# Fritzing sketch digispark_usb_isp (saved by Fritzing 1.0.5)

parts:
  Bauteil1 = Arduino Uno (Rev3)
  Mod1 = Digispark

nets:
  N1: Bauteil1.D10_PWM/SS, Mod1.P5
  N2: Bauteil1.D11_PWM/MOSI, Mod1.P0
  N3: Bauteil1.D12/MISO, Mod1.P1
  N4: Bauteil1.D13/SCK, Mod1.P2
  GND: Bauteil1.GND, Mod1.GND
  5V: Bauteil1.5V, Mod1.VCC

custom parts:
  Digispark: The Digispark is an Attiny85 based microcontroller development board similar to the Arduino line, only cheaper, smaller, and a bit less powerful. With a whole host of shields to extend its functionality and the ability to use the familiar Arduino IDE the Digispark is a great way to jump into electronics, or perfect for when an Arduino is too big or too much. May 2019 modified to correct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
