# Fritzing sketch circuit_diagram (saved by Fritzing 1.0.5)

parts:
  A1 = MH-ET Live Minikit for ESP32
  Mod1 = Digispark
  U1 = WS2812 RGB LED strip
  Bauteil1 = Adafruit USB Type C Breakout [part_number=4090]

nets:
  GND: A1.GND, Mod1.GND, U1.GND, Bauteil1.GND
  N1: A1.RST, Mod1.P0
  N2: A1.IO16, Mod1.P3, U1.DIN
  VCC: A1.VCC, Mod1.VCC, U1.VCC, Bauteil1.VBUS
  N3: Mod1.P2, Bauteil1.CC1
  N4: Mod1.P4, Bauteil1.CC2

custom parts:
  MH-ET Live Minikit for ESP32: MH-ET Live Minikit for ESP32 ( http://mh.nodebb.com/topic/8/mh-et-live-minikit-for-esp32/2/) PCB footprint is invalid.
  Digispark: The Digispark is an Attiny85 based microcontroller development board similar to the Arduino line, only cheaper, smaller, and a bit less powerful. With a whole host of shields to extend its functionality and the ability to use the familiar Arduino IDE the Digispark is a great way to jump into electronics, or perfect for when an Arduino is too big or too much. May 2019 modified to correct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
  WS2812 RGB LED strip: WS2812 strip
  Adafruit USB Type C Breakout: Adafruit breakout board for USB Type C socket.
